# Fritzing sketch blink_schem (saved by Fritzing 0.9.4)
breadboards: 1

parts:
  LED1 = LED - 5mm [color="Red (633nm)" package="5 mm [THT]"]
  R1 = Resistor [tolerance=±5% resistance=220 package=THT]

nets:
  GND/ground: LED1.cathode
  N1: LED1.anode, R1.Pin_1
  GPIO 21: R1.Pin_0

notes:
  Anode
  Cathode
  (long lead)
