# Fritzing sketch button_blink_bb (saved by Fritzing 0.9.4)
breadboards: 1

parts:
  Raspberry_Pi_1 = Raspberry Pi 3 [part_number=RPI-3-V1.2]
  LED1 = LED - 5mm [color="Red (633nm)" package="5 mm [THT]"]
  R1 = Resistor [tolerance=±5% resistance=220 package=THT]
  S1 = Pushbutton [package="[THT]"]

nets:
  N1: Raspberry_Pi_1.GIPO26, S1.Pin_3, S1.Pin_4
  N2: Raspberry_Pi_1.GIPO21, R1.Pin_0
  N3: Raspberry_Pi_1.GND, LED1.cathode, S1.Pin_1, S1.Pin_2
  N4: LED1.anode, R1.Pin_1
