# Fritzing sketch button_blink_schem (saved by Fritzing 0.9.4)
breadboards: 1

parts:
  LED1 = LED - 5mm [color="Red (633nm)" package="5 mm [THT]"]
  R1 = Resistor [tolerance=±5% resistance=220 package=THT]
  S1 = SWITCH-MOMENTARY-2 [package=tactile_switch_tall]

nets:
  GND/ground: LED1.cathode, S1.1
  N1: LED1.anode, R1.Pin_1
  GPIO 21: R1.Pin_0
  GPIO 26: S1.2

notes:
  Anode
  Cathode
  (long lead)
